# Fritzing sketch TrafikklysKrets (saved by Fritzing 0.9.3b)
breadboards: 1

parts:
  R1 = Resistor [tolerance=±5% resistance=220 package=THT]
  R2 = Resistor [tolerance=±5% resistance=220 package=THT]
  R3 = Resistor [tolerance=±5% resistance=220 package=THT]
  R4 = Resistor [tolerance=±5% resistance=220 package=THT]
  R5 = Resistor [tolerance=±5% resistance=220 package=THT]
  S1 = Pushbutton [package="[THT]"]
  R6 = Resistor [tolerance=±5% resistance=220 package=THT]
  Part1 = Arduino Uno (Rev3)
  LED1 = LED - 5mm [color="Red (635nm)" package="5 mm [THT]"]
  LED2 = LED - 5mm [color="Green (570nm)" package="5 mm [THT]"]
  LED5 = LED - 5mm [color="Red (633nm)" package="5 mm [THT]"]
  LED6 = LED - 5mm [color="Green (570nm)" package="5 mm [THT]"]
  LED7 = LED - 5mm [color="Yellow (585nm)" package="5 mm [THT]"]
  R7 = Resistor [tolerance=±5% resistance=10k package="2010 [SMD]"]
  J1 = Basic Servo

nets:
  N1: R1.Pin_0, Part1.D13/SCK
  N2: R1.Pin_1, LED1.cathode
  N3: R2.Pin_0, Part1.D12/MISO
  N4: R2.Pin_1, LED2.cathode
  N5: R3.Pin_0, Part1.D10_PWM/SS
  N6: R3.Pin_1, LED5.cathode
  N7: R4.Pin_0, Part1.D9_PWM
  N8: R4.Pin_1, LED7.cathode
  N9: R5.Pin_0, Part1.D8
  N10: R5.Pin_1, LED6.cathode
  N11: S1.Pin_1, S1.Pin_2, R6.Pin_0, R7.Pin_0
  N12: S1.Pin_3, S1.Pin_4
  N13: R6.Pin_1, Part1.D2
  GND: Part1.GND, LED1.anode, LED2.anode, LED5.anode, LED6.anode, LED7.anode, J1.gnd
  N14: Part1.D7, J1.pulse
  5V: Part1.5V, R7.Pin_1, J1.vcc
